# Fritzing sketch SmartRoomControllerCircuitry (saved by Fritzing 0.9.4)
breadboards: 3

parts:
  Teensy_3_1 = Teensy 3.1  # not connected
  WIZ820io1 = WIZ820io [part_number=WIZ820io]
  S1 = Pushbutton [package="[THT]"]
  S2 = Pushbutton [package="[THT]"]
  RG_encoder1 = SprkFn RG Encoder [package="DIP (Dual Inline) [THT]"]
  Part1 = 12 NeoPixel Ring [part_number=1643]
  M1 = BMP280
  OLED_I2C1 = OLED 128x64 I2C Monochrome Display
  Part2 = Adafruit MicroSD card breakout board [part_number="Adafruit #254"]
  R1 = Resistor [tolerance=±5% resistance=220 package=THT]
  R2 = Resistor [tolerance=±5% resistance=220 package=THT]

nets:
  GND: WIZ820io1.GND, RG_encoder1.GND, RG_encoder1.C, Part1.GND, M1.GND, OLED_I2C1.GND, Part2.GND, R1.Pin_0, R2.Pin_0
  N1: WIZ820io1.MOSI, Part2.DI
  N2: WIZ820io1.SCLK, Part2.CLK
  N3: WIZ820io1.MISO, Part2.DO
  VIN: WIZ820io1.VIN, S1.Pin_3, S1.Pin_4, S2.Pin_3, S2.Pin_4, Part1.VDD, M1.VIN, OLED_I2C1.VDD, Part2.VCC
  N4: S1.Pin_1, S1.Pin_2, R1.Pin_1
  N5: S2.Pin_1, S2.Pin_2, RG_encoder1.SW, R2.Pin_1
  N6: M1.SCL, OLED_I2C1.SCK
  N7: M1.SDA, OLED_I2C1.SDA

custom parts:
  Pushbutton: A generic pushbutton.
  Pushbutton: A generic pushbutton.
  SprkFn RG Encoder: SparkFun RG Rotary Encoder
  12 NeoPixel Ring: 12 ultra bright smart LED NeoPixels are arranged in a circle with 1.5" (37mm) outer diameter. The rings are 'chainable' - connect the output pin of one to the input pin of another. Use only one microcontroller pin to control as many as you can chain together! Each LED is addressable as the driver chip is inside the LED. Each one has ~18mA constant current drive so the color will be very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
  BMP280: Temperature Humidity Barometric presure Sensor, I2C
  Adafruit MicroSD card breakout board: Not just a simple breakout board, this microSD adapter goes the extra mile - designed for ease of use. Onboard 5v->3v regulator provides 150mA for power-hungry cards 3v level shifting means you can use this with ease on either 3v or 5v systems Uses a proper level shifting chip, not resistors: less problems, and faster read/write access Use 3 or 4 digital pins to read and write 2Gb+ of storage!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
